// Digital circuit 6502.dig as structural Verilog
module _6502 (
  input  Clock,
  input  [2:0] ALU_Control,
  input  [7:0] Data_In,
  input  Reset,
  input  [15:0] Addr_In,
  input  Inc,
  input  Dec,
  input  Jump,
  input  Count,
  input  [1:0] Chip_Select,
  input  R_W,
  input  Addr_IO,
  input  Data_IO,
  input  B_En,
  input  A_En,
  input  [7:0] A,
  input  [7:0] B,
  output out_2,
  output out_4,
  output [7:0] Data_Out,
  output [15:0] Addr_Out,
  output out_14,
  output out_16
);

  wire PC_CS, SP_CS;
  wire [7:0] driverinvsel_2_out, register_1_q, register_2_q;
  wire [15:0] driver_1_out;

  Decoder #(.Selector_Bits(2)) decoder_1 (.sel(Chip_Select), .out_0(PC_CS), .out_1(SP_CS));  // open: out_2, out_3
  StackPointer_6502 stackpointer_6502_1 ();
  ProgramCounter_6502 programcounter_6502_1 ();
  assign driver_1_out = Addr_IO ? Addr_In : 16'bz;  // Driver driver_1
  assign Addr_Out = ~Addr_IO ? driver_1_out : 16'bz;  // DriverInvSel driverinvsel_1
  ALU_6502 alu_6502_1 ();
  Register #(.Bits(8)) register_1 (.D(A), .C(Clock), .en(A_En), .Q(register_1_q));
  Register #(.Bits(8)) register_2 (.D(B), .C(Clock), .en(B_En), .Q(register_2_q));
  assign driverinvsel_2_out = ~Data_IO ? Data_In : 8'bz;  // DriverInvSel driverinvsel_2
  assign Data_Out = Data_IO ? driverinvsel_2_out : 8'bz;  // Driver driver_2
endmodule
