// Digital circuit ALU_6502.dig as structural Verilog
module ALU_6502 (
  input  [7:0] A,
  input  [7:0] B,
  input  [2:0] Control,
  output [7:0] Data,
  output Carry,
  output Zero
);

  wire add_1_c_o, add_2_c_o, add_3_c_o, add_4_c_o, add_6_c_o, add_7_c_o, add_8_c_o, and_9_out, and_10_out,
       and_12_out, and_13_out, and_14_out, and_15_out, and_16_out, and_17_out, and_18_out, and_19_out,
       and_20_out, and_21_out, and_23_out, CS_ADD, CS_AND, CS_LEFT, CS_OR, CS_RIGHT, CS_SUB, CS_XOR,
       not_1_out, not_2_out, or_11_out, or_12_out, or_13_out, or_14_out, or_16_out, or_17_out, or_18_out,
       xor_1_out, xor_2_out, xor_4_out, xor_8_out, xor_12_out, xor_14_out, xor_15_out, xor_16_out,
       xor_17_out, xor_18_out;
  wire [7:0] add_1_s, and_1_out, and_11_out, or_1_out, xor_3_out;

  // Probe Binary on A
  // Probe Hex on A
  // Probe Binary on B
  // Probe Hex on B
  Decoder #(.Selector_Bits(3)) decoder_1 (
    .sel(Control), .out_0(CS_ADD), .out_1(CS_SUB), .out_2(CS_AND), .out_3(CS_OR), .out_4(CS_XOR),
    .out_5(CS_LEFT), .out_6(CS_RIGHT));  // open: out_7
  xor xor_1 (xor_1_out, B[0], CS_SUB);
  xor xor_2 (xor_2_out, B[1], CS_SUB);
  and and_1 (and_1_out[0], A[0], B[0]);
  or or_1 (or_1_out[0], A[0], B[0]);
  xor xor_3 (xor_3_out[0], A[0], B[0]);
  Add add_1 (.a(A[0]), .b(xor_1_out), .c_i(CS_SUB), .s(add_1_s[0]), .c_o(add_1_c_o));
  Add add_2 (.a(A[1]), .b(xor_2_out), .c_i(add_1_c_o), .s(add_1_s[1]), .c_o(add_2_c_o));
  Add add_3 (.a(A[2]), .b(xor_4_out), .c_i(add_2_c_o), .s(add_1_s[2]), .c_o(add_3_c_o));
  Add add_4 (.a(A[3]), .b(xor_8_out), .c_i(add_3_c_o), .s(add_1_s[3]), .c_o(add_4_c_o));
  xor xor_4 (xor_4_out, B[2], CS_SUB);
  and and_2 (and_1_out[2], A[2], B[2]);
  and and_3 (and_1_out[4], A[4], B[4]);
  and and_4 (and_1_out[6], A[6], B[6]);
  or or_2 (or_1_out[2], A[2], B[2]);
  or or_3 (or_1_out[4], A[4], B[4]);
  or or_4 (or_1_out[6], A[6], B[6]);
  xor xor_5 (xor_3_out[2], A[2], B[2]);
  xor xor_6 (xor_3_out[4], A[4], B[4]);
  xor xor_7 (xor_3_out[6], A[6], B[6]);
  xor xor_8 (xor_8_out, B[3], CS_SUB);
  and and_5 (and_1_out[1], A[1], B[1]);
  and and_6 (and_1_out[3], A[3], B[3]);
  and and_7 (and_1_out[5], A[5], B[5]);
  or or_5 (or_1_out[1], A[1], B[1]);
  or or_6 (or_1_out[3], A[3], B[3]);
  or or_7 (or_1_out[5], A[5], B[5]);
  xor xor_9 (xor_3_out[1], A[1], B[1]);
  xor xor_10 (xor_3_out[3], A[3], B[3]);
  xor xor_11 (xor_3_out[5], A[5], B[5]);
  xor xor_12 (xor_12_out, B[4], CS_SUB);
  and and_8 (and_1_out[7], A[7], B[7]);
  or or_8 (or_1_out[7], A[7], B[7]);
  xor xor_13 (xor_3_out[7], A[7], B[7]);
  xor xor_14 (xor_14_out, B[5], CS_SUB);
  xor xor_15 (xor_15_out, B[6], CS_SUB);
  Add add_5 (.a(A[7]), .b(xor_16_out), .c_i(add_6_c_o), .s(add_1_s[7]), .c_o(Carry));
  Add add_6 (.a(A[6]), .b(xor_15_out), .c_i(add_7_c_o), .s(add_1_s[6]), .c_o(add_6_c_o));
  Add add_7 (.a(A[5]), .b(xor_14_out), .c_i(add_8_c_o), .s(add_1_s[5]), .c_o(add_7_c_o));
  Add add_8 (.a(A[4]), .b(xor_12_out), .c_i(add_4_c_o), .s(add_1_s[4]), .c_o(add_8_c_o));
  xor xor_16 (xor_16_out, B[7], CS_SUB);
  assign Data = CS_AND ? and_1_out : 8'bz;  // Driver driver_1
  assign Data = CS_OR ? or_1_out : 8'bz;  // Driver driver_2
  assign Data = CS_XOR ? xor_3_out : 8'bz;  // Driver driver_3
  not not_1 (not_1_out, and_9_out);
  assign Data = xor_17_out ? and_11_out : 8'bz;  // Driver driver_4
  assign Data = xor_18_out ? add_1_s : 8'bz;  // Driver driver_5
  and and_9 (and_9_out, CS_LEFT, not_2_out);
  and and_10 (and_10_out, and_9_out, A[0]);
  xor xor_17 (xor_17_out, CS_RIGHT, CS_LEFT);
  xor xor_18 (xor_18_out, CS_ADD, CS_SUB);
  not not_2 (not_2_out, CS_RIGHT);
  and and_11 (and_11_out[0], A[1], not_1_out);
  or or_9 (and_11_out[1], and_13_out, and_10_out);
  and and_12 (and_12_out, and_9_out, A[1]);
  and and_13 (and_13_out, A[2], not_1_out);
  and and_14 (and_14_out, and_9_out, A[2]);
  or or_10 (and_11_out[2], and_15_out, and_12_out);
  or or_11 (or_11_out, Data[3], or_12_out);
  or or_12 (or_12_out, Data[2], or_13_out);
  or or_13 (or_13_out, Data[1], Data[0]);
  and and_15 (and_15_out, A[3], not_1_out);
  or or_14 (or_14_out, Data[7], or_16_out);
  and and_16 (and_16_out, and_9_out, A[3]);
  or or_15 (and_11_out[3], and_17_out, and_14_out);
  not not_3 (Zero, or_14_out);
  or or_16 (or_16_out, or_17_out, Data[6]);
  or or_17 (or_17_out, or_18_out, Data[5]);
  or or_18 (or_18_out, or_11_out, Data[4]);
  and and_17 (and_17_out, A[4], not_1_out);
  or or_19 (and_11_out[4], and_19_out, and_16_out);
  and and_18 (and_18_out, and_9_out, A[4]);
  and and_19 (and_19_out, A[5], not_1_out);
  or or_20 (and_11_out[5], and_21_out, and_18_out);
  and and_20 (and_20_out, and_9_out, A[5]);
  // Probe Binary on Data
  // Probe Hex on Data
  and and_21 (and_21_out, A[6], not_1_out);
  and and_22 (and_11_out[7], and_9_out, A[6]);
  or or_21 (and_11_out[6], and_23_out, and_20_out);
  and and_23 (and_23_out, A[7], not_1_out);

  // Notes on the sheet:
  //   Control: [ 0 - Add ]   
  //   [ 1 - Sub ]   
  //   [ 2 - And]   
  //   [ 3 - Or ]   
  //   [ 4 - Xor ]   
  //   [ 5 - Left Shift ]   
  //   [ 6 - Right Shift ]   
  //   [ 7 - Undefined ]
  //   ADD/SUB
  //   AND
  //   OR
  //   XOR
  //   BIT SHIFT
  //   ZERO
endmodule
