// Digital circuit ProgramCounter_6502.dig as structural Verilog
module ProgramCounter_6502 (
  input  Jump,
  input  Count,
  input  Clock,
  input  Reset,
  input  CS,
  output [15:0] Addr,
  output Carry
);

  wire and_1_out, and_2_out, and_3_out, and_4_out, and_5_out, and_6_out, and_7_out, and_8_out, and_9_out,
       and_10_out, and_11_out, and_12_out, and_13_out, and_14_out, and_15_out, and_16_out, and_17_out,
       and_18_out, and_19_out, and_20_out, and_21_out, and_22_out, and_23_out, and_24_out, and_25_out,
       and_26_out, and_27_out, and_28_out, and_29_out, and_30_out, and_31_out, and_32_out, and_33_out,
       and_34_out, and_35_out, and_36_out, and_37_out, and_38_out, and_39_out, and_40_out, and_41_out,
       and_42_out, and_43_out, and_44_out, and_45_out, and_46_out, and_47_out, and_48_out, and_49_out,
       and_50_out, and_51_out, and_52_out, and_53_out, and_54_out, and_55_out, and_56_out, and_57_out,
       and_58_out, and_59_out, and_60_out, and_61_out, and_63_out, and_64_out, and_65_out, and_66_out,
       nor_1_out, nor_2_out, nor_4_out, nor_5_out, nor_6_out, nor_7_out, nor_8_out, nor_9_out, nor_11_out,
       nor_12_out, nor_13_out, nor_14_out, nor_15_out, nor_16_out, nor_18_out, nor_19_out, nor_20_out,
       nor_21_out, nor_22_out, nor_23_out, nor_25_out, nor_26_out, nor_27_out, nor_28_out, nor_29_out,
       nor_30_out, nor_32_out, nor_33_out, nor_34_out, nor_35_out, nor_36_out, nor_37_out, nor_39_out,
       nor_40_out, nor_41_out, nor_42_out, nor_43_out, nor_44_out, nor_46_out, nor_47_out, nor_48_out,
       nor_49_out, nor_50_out, nor_51_out, nor_53_out, nor_54_out, nor_55_out, nor_56_out, nor_57_out,
       nor_58_out, nor_60_out, nor_61_out, nor_62_out, nor_63_out, nor_64_out, nor_65_out, nor_67_out,
       nor_68_out, nor_69_out, nor_70_out, nor_71_out, nor_72_out, nor_74_out, nor_75_out, nor_76_out,
       nor_77_out, nor_78_out, nor_79_out, nor_81_out, nor_82_out, nor_83_out, nor_84_out, nor_85_out,
       nor_86_out, nor_88_out, nor_89_out, nor_90_out, nor_91_out, nor_92_out, nor_93_out, nor_95_out,
       nor_96_out, nor_97_out, nor_98_out, nor_99_out, nor_100_out, nor_102_out, nor_103_out, nor_104_out,
       nor_105_out, nor_106_out, nor_107_out, nor_109_out, nor_110_out, nor_111_out, nor_112_out, or_1_out,
       xor_1_out, xor_2_out, xor_3_out, xor_4_out, xor_5_out, xor_6_out, xor_7_out, xor_8_out, xor_9_out,
       xor_10_out, xor_11_out, xor_12_out, xor_13_out, xor_14_out, xor_15_out, xor_16_out;
  wire [15:0] driverinvsel_1_out, nor_3_out;

  and and_1 (and_1_out, CS, ~Jump);  // And
  and and_2 (and_2_out, CS, Jump);
  or or_1 (or_1_out, Jump, Count, Reset);
  assign driverinvsel_1_out = ~Jump ? nor_3_out : 16'bz;  // DriverInvSel driverinvsel_1
  and and_3 (and_3_out, Count, driverinvsel_1_out[0]);
  xor xor_1 (xor_1_out, Count, driverinvsel_1_out[0]);
  assign Addr = and_1_out ? driverinvsel_1_out : 16'bz;  // Driver driver_1
  assign driverinvsel_1_out = and_2_out ? Addr : 16'bz;  // Driver driver_2
  and and_4 (and_4_out, or_1_out, xor_1_out);
  nor nor_1 (nor_1_out, nor_5_out, Clock);
  nor nor_2 (nor_2_out, nor_6_out, nor_1_out);
  and and_5 (and_5_out, Clock, nor_2_out);
  nor nor_3 (nor_3_out[0], nor_7_out, and_5_out);
  and and_6 (and_6_out, and_3_out, driverinvsel_1_out[1]);
  xor xor_2 (xor_2_out, and_3_out, driverinvsel_1_out[1]);
  nor nor_4 (nor_4_out, nor_7_out, or_1_out);
  nor nor_5 (nor_5_out, nor_4_out, and_4_out, Clock);
  nor nor_6 (nor_6_out, nor_5_out, Reset, nor_2_out);
  and and_7 (and_7_out, nor_6_out, Clock);
  nor nor_7 (nor_7_out, and_7_out, nor_3_out[0]);
  and and_8 (and_8_out, or_1_out, xor_2_out);
  nor nor_8 (nor_8_out, nor_12_out, Clock);
  nor nor_9 (nor_9_out, nor_13_out, nor_8_out);
  and and_9 (and_9_out, Clock, nor_9_out);
  nor nor_10 (nor_3_out[1], nor_14_out, and_9_out);
  and and_10 (and_10_out, and_6_out, driverinvsel_1_out[2]);
  xor xor_3 (xor_3_out, and_6_out, driverinvsel_1_out[2]);
  nor nor_11 (nor_11_out, nor_14_out, or_1_out);
  nor nor_12 (nor_12_out, nor_11_out, and_8_out, Clock);
  nor nor_13 (nor_13_out, nor_12_out, Reset, nor_9_out);
  and and_11 (and_11_out, nor_13_out, Clock);
  nor nor_14 (nor_14_out, and_11_out, nor_3_out[1]);
  and and_12 (and_12_out, or_1_out, xor_3_out);
  nor nor_15 (nor_15_out, nor_19_out, Clock);
  nor nor_16 (nor_16_out, nor_20_out, nor_15_out);
  and and_13 (and_13_out, Clock, nor_16_out);
  nor nor_17 (nor_3_out[2], nor_21_out, and_13_out);
  and and_14 (and_14_out, and_10_out, driverinvsel_1_out[3]);
  xor xor_4 (xor_4_out, and_10_out, driverinvsel_1_out[3]);
  nor nor_18 (nor_18_out, nor_21_out, or_1_out);
  nor nor_19 (nor_19_out, nor_18_out, and_12_out, Clock);
  nor nor_20 (nor_20_out, nor_19_out, Reset, nor_16_out);
  and and_15 (and_15_out, nor_20_out, Clock);
  nor nor_21 (nor_21_out, and_15_out, nor_3_out[2]);
  and and_16 (and_16_out, or_1_out, xor_4_out);
  nor nor_22 (nor_22_out, nor_26_out, Clock);
  nor nor_23 (nor_23_out, nor_27_out, nor_22_out);
  and and_17 (and_17_out, Clock, nor_23_out);
  nor nor_24 (nor_3_out[3], nor_28_out, and_17_out);
  and and_18 (and_18_out, and_14_out, driverinvsel_1_out[4]);
  xor xor_5 (xor_5_out, and_14_out, driverinvsel_1_out[4]);
  nor nor_25 (nor_25_out, nor_28_out, or_1_out);
  nor nor_26 (nor_26_out, nor_25_out, and_16_out, Clock);
  nor nor_27 (nor_27_out, nor_26_out, Reset, nor_23_out);
  and and_19 (and_19_out, nor_27_out, Clock);
  nor nor_28 (nor_28_out, and_19_out, nor_3_out[3]);
  and and_20 (and_20_out, or_1_out, xor_5_out);
  nor nor_29 (nor_29_out, nor_33_out, Clock);
  nor nor_30 (nor_30_out, nor_34_out, nor_29_out);
  and and_21 (and_21_out, Clock, nor_30_out);
  nor nor_31 (nor_3_out[4], nor_35_out, and_21_out);
  and and_22 (and_22_out, and_18_out, driverinvsel_1_out[5]);
  xor xor_6 (xor_6_out, and_18_out, driverinvsel_1_out[5]);
  nor nor_32 (nor_32_out, nor_35_out, or_1_out);
  nor nor_33 (nor_33_out, nor_32_out, and_20_out, Clock);
  nor nor_34 (nor_34_out, nor_33_out, Reset, nor_30_out);
  and and_23 (and_23_out, nor_34_out, Clock);
  nor nor_35 (nor_35_out, and_23_out, nor_3_out[4]);
  and and_24 (and_24_out, or_1_out, xor_6_out);
  nor nor_36 (nor_36_out, nor_40_out, Clock);
  nor nor_37 (nor_37_out, nor_41_out, nor_36_out);
  and and_25 (and_25_out, Clock, nor_37_out);
  nor nor_38 (nor_3_out[5], nor_42_out, and_25_out);
  and and_26 (and_26_out, and_22_out, driverinvsel_1_out[6]);
  xor xor_7 (xor_7_out, and_22_out, driverinvsel_1_out[6]);
  nor nor_39 (nor_39_out, nor_42_out, or_1_out);
  nor nor_40 (nor_40_out, nor_39_out, and_24_out, Clock);
  nor nor_41 (nor_41_out, nor_40_out, Reset, nor_37_out);
  and and_27 (and_27_out, nor_41_out, Clock);
  nor nor_42 (nor_42_out, and_27_out, nor_3_out[5]);
  and and_28 (and_28_out, or_1_out, xor_7_out);
  nor nor_43 (nor_43_out, nor_47_out, Clock);
  nor nor_44 (nor_44_out, nor_48_out, nor_43_out);
  and and_29 (and_29_out, Clock, nor_44_out);
  nor nor_45 (nor_3_out[6], nor_49_out, and_29_out);
  and and_30 (and_30_out, and_26_out, driverinvsel_1_out[7]);
  xor xor_8 (xor_8_out, and_26_out, driverinvsel_1_out[7]);
  nor nor_46 (nor_46_out, nor_49_out, or_1_out);
  nor nor_47 (nor_47_out, nor_46_out, and_28_out, Clock);
  nor nor_48 (nor_48_out, nor_47_out, Reset, nor_44_out);
  and and_31 (and_31_out, nor_48_out, Clock);
  nor nor_49 (nor_49_out, and_31_out, nor_3_out[6]);
  and and_32 (and_32_out, or_1_out, xor_8_out);
  nor nor_50 (nor_50_out, nor_54_out, Clock);
  nor nor_51 (nor_51_out, nor_55_out, nor_50_out);
  and and_33 (and_33_out, Clock, nor_51_out);
  nor nor_52 (nor_3_out[7], nor_56_out, and_33_out);
  and and_34 (and_34_out, and_30_out, driverinvsel_1_out[8]);
  xor xor_9 (xor_9_out, and_30_out, driverinvsel_1_out[8]);
  nor nor_53 (nor_53_out, nor_56_out, or_1_out);
  nor nor_54 (nor_54_out, nor_53_out, and_32_out, Clock);
  nor nor_55 (nor_55_out, nor_54_out, Reset, nor_51_out);
  and and_35 (and_35_out, nor_55_out, Clock);
  nor nor_56 (nor_56_out, and_35_out, nor_3_out[7]);
  and and_36 (and_36_out, or_1_out, xor_9_out);
  nor nor_57 (nor_57_out, nor_61_out, Clock);
  nor nor_58 (nor_58_out, nor_62_out, nor_57_out);
  and and_37 (and_37_out, Clock, nor_58_out);
  nor nor_59 (nor_3_out[8], nor_63_out, and_37_out);
  and and_38 (and_38_out, and_34_out, driverinvsel_1_out[9]);
  xor xor_10 (xor_10_out, and_34_out, driverinvsel_1_out[9]);
  nor nor_60 (nor_60_out, nor_63_out, or_1_out);
  nor nor_61 (nor_61_out, nor_60_out, and_36_out, Clock);
  nor nor_62 (nor_62_out, nor_61_out, Reset, nor_58_out);
  and and_39 (and_39_out, nor_62_out, Clock);
  nor nor_63 (nor_63_out, and_39_out, nor_3_out[8]);
  and and_40 (and_40_out, or_1_out, xor_10_out);
  nor nor_64 (nor_64_out, nor_68_out, Clock);
  nor nor_65 (nor_65_out, nor_69_out, nor_64_out);
  and and_41 (and_41_out, Clock, nor_65_out);
  nor nor_66 (nor_3_out[9], nor_70_out, and_41_out);
  and and_42 (and_42_out, and_38_out, driverinvsel_1_out[10]);
  xor xor_11 (xor_11_out, and_38_out, driverinvsel_1_out[10]);
  nor nor_67 (nor_67_out, nor_70_out, or_1_out);
  nor nor_68 (nor_68_out, nor_67_out, and_40_out, Clock);
  nor nor_69 (nor_69_out, nor_68_out, Reset, nor_65_out);
  and and_43 (and_43_out, nor_69_out, Clock);
  nor nor_70 (nor_70_out, and_43_out, nor_3_out[9]);
  and and_44 (and_44_out, or_1_out, xor_11_out);
  nor nor_71 (nor_71_out, nor_75_out, Clock);
  nor nor_72 (nor_72_out, nor_76_out, nor_71_out);
  and and_45 (and_45_out, Clock, nor_72_out);
  nor nor_73 (nor_3_out[10], nor_77_out, and_45_out);
  and and_46 (and_46_out, and_42_out, driverinvsel_1_out[11]);
  xor xor_12 (xor_12_out, and_42_out, driverinvsel_1_out[11]);
  nor nor_74 (nor_74_out, nor_77_out, or_1_out);
  nor nor_75 (nor_75_out, nor_74_out, and_44_out, Clock);
  nor nor_76 (nor_76_out, nor_75_out, Reset, nor_72_out);
  and and_47 (and_47_out, nor_76_out, Clock);
  nor nor_77 (nor_77_out, and_47_out, nor_3_out[10]);
  and and_48 (and_48_out, or_1_out, xor_12_out);
  nor nor_78 (nor_78_out, nor_82_out, Clock);
  nor nor_79 (nor_79_out, nor_83_out, nor_78_out);
  and and_49 (and_49_out, Clock, nor_79_out);
  nor nor_80 (nor_3_out[11], nor_84_out, and_49_out);
  and and_50 (and_50_out, and_46_out, driverinvsel_1_out[12]);
  xor xor_13 (xor_13_out, and_46_out, driverinvsel_1_out[12]);
  nor nor_81 (nor_81_out, nor_84_out, or_1_out);
  nor nor_82 (nor_82_out, nor_81_out, and_48_out, Clock);
  nor nor_83 (nor_83_out, nor_82_out, Reset, nor_79_out);
  and and_51 (and_51_out, nor_83_out, Clock);
  nor nor_84 (nor_84_out, and_51_out, nor_3_out[11]);
  and and_52 (and_52_out, or_1_out, xor_13_out);
  nor nor_85 (nor_85_out, nor_89_out, Clock);
  nor nor_86 (nor_86_out, nor_90_out, nor_85_out);
  and and_53 (and_53_out, Clock, nor_86_out);
  nor nor_87 (nor_3_out[12], nor_91_out, and_53_out);
  and and_54 (and_54_out, and_50_out, driverinvsel_1_out[13]);
  xor xor_14 (xor_14_out, and_50_out, driverinvsel_1_out[13]);
  nor nor_88 (nor_88_out, nor_91_out, or_1_out);
  nor nor_89 (nor_89_out, nor_88_out, and_52_out, Clock);
  nor nor_90 (nor_90_out, nor_89_out, Reset, nor_86_out);
  and and_55 (and_55_out, nor_90_out, Clock);
  nor nor_91 (nor_91_out, and_55_out, nor_3_out[12]);
  and and_56 (and_56_out, or_1_out, xor_14_out);
  nor nor_92 (nor_92_out, nor_96_out, Clock);
  nor nor_93 (nor_93_out, nor_97_out, nor_92_out);
  and and_57 (and_57_out, Clock, nor_93_out);
  nor nor_94 (nor_3_out[13], nor_98_out, and_57_out);
  and and_58 (and_58_out, and_54_out, driverinvsel_1_out[14]);
  xor xor_15 (xor_15_out, and_54_out, driverinvsel_1_out[14]);
  nor nor_95 (nor_95_out, nor_98_out, or_1_out);
  nor nor_96 (nor_96_out, nor_95_out, and_56_out, Clock);
  nor nor_97 (nor_97_out, nor_96_out, Reset, nor_93_out);
  and and_59 (and_59_out, nor_97_out, Clock);
  nor nor_98 (nor_98_out, and_59_out, nor_3_out[13]);
  and and_60 (and_60_out, or_1_out, xor_15_out);
  nor nor_99 (nor_99_out, nor_103_out, Clock);
  nor nor_100 (nor_100_out, nor_104_out, nor_99_out);
  and and_61 (and_61_out, Clock, nor_100_out);
  nor nor_101 (nor_3_out[14], nor_105_out, and_61_out);
  and and_62 (Carry, and_58_out, driverinvsel_1_out[15]);
  xor xor_16 (xor_16_out, and_58_out, driverinvsel_1_out[15]);
  nor nor_102 (nor_102_out, nor_105_out, or_1_out);
  nor nor_103 (nor_103_out, nor_102_out, and_60_out, Clock);
  nor nor_104 (nor_104_out, nor_103_out, Reset, nor_100_out);
  and and_63 (and_63_out, nor_104_out, Clock);
  nor nor_105 (nor_105_out, and_63_out, nor_3_out[14]);
  and and_64 (and_64_out, or_1_out, xor_16_out);
  nor nor_106 (nor_106_out, nor_110_out, Clock);
  nor nor_107 (nor_107_out, nor_111_out, nor_106_out);
  and and_65 (and_65_out, Clock, nor_107_out);
  nor nor_108 (nor_3_out[15], nor_112_out, and_65_out);
  nor nor_109 (nor_109_out, nor_112_out, or_1_out);
  nor nor_110 (nor_110_out, nor_109_out, and_64_out, Clock);
  nor nor_111 (nor_111_out, nor_110_out, Reset, nor_107_out);
  and and_66 (and_66_out, nor_111_out, Clock);
  nor nor_112 (nor_112_out, and_66_out, nor_3_out[15]);
endmodule
