// Digital circuit StackPointer_6502.dig as structural Verilog
module StackPointer_6502 (
  input  Inc,
  input  Dec,
  input  Reset,
  input  Clock,
  input  CS,
  input  R_W,
  output [15:0] Addr,
  output Carry
);

  wire and_1_out, and_2_out, and_3_out, and_4_out, and_5_out, and_6_out, and_7_out, and_8_out, and_9_out,
       and_10_out, and_11_out, and_12_out, and_13_out, and_14_out, and_15_out, and_16_out, and_17_out,
       and_18_out, and_19_out, and_20_out, and_21_out, and_22_out, and_23_out, and_24_out, and_26_out,
       nor_1_out, nor_2_out, nor_4_out, nor_5_out, nor_6_out, nor_7_out, nor_8_out, nor_10_out, nor_11_out,
       nor_12_out, nor_13_out, nor_14_out, nor_16_out, nor_17_out, nor_18_out, nor_19_out, nor_20_out,
       nor_22_out, nor_23_out, nor_24_out, nor_25_out, nor_26_out, nor_28_out, nor_29_out, nor_30_out,
       nor_31_out, nor_32_out, nor_34_out, nor_35_out, nor_36_out, nor_37_out, nor_38_out, nor_40_out,
       nor_41_out, nor_42_out, nor_43_out, nor_44_out, nor_46_out, nor_47_out, nor_48_out, or_1_out,
       xor_1_out, xor_2_out, xor_3_out, xor_4_out, xor_5_out, xor_6_out, xor_7_out, xor_8_out, xor_9_out,
       xor_10_out, xor_11_out, xor_12_out, xor_13_out, xor_14_out, xor_15_out, xor_16_out;
  wire [7:0] nor_3_out, pulldown_1_out;
  wire [15:0] driver_1_out;

  or or_1 (or_1_out, Inc, Dec);
  and and_1 (and_1_out, CS, R_W);
  assign driver_1_out = and_1_out ? Addr : 16'bz;  // Driver driver_1
  assign Addr = and_2_out ? driver_1_out : 16'bz;  // Driver driver_2
  and and_2 (and_2_out, CS, ~R_W);  // And
  assign driver_1_out = and_2_out ? {pulldown_1_out, nor_3_out} : 16'bz;  // Driver driver_3
  PullDown #(.Bits(8)) pulldown_1 (.out(pulldown_1_out));
  xor xor_1 (xor_1_out, driver_1_out[0], Dec);
  and and_3 (and_3_out, xor_1_out, or_1_out);
  nor nor_1 (nor_1_out, nor_4_out, Clock);
  nor nor_2 (nor_2_out, nor_5_out, nor_1_out);
  and and_4 (and_4_out, Clock, nor_2_out);
  nor nor_3 (nor_3_out[0], nor_6_out, and_4_out);
  PullDown #(.Bits(8)) pulldown_2 (.out(driver_1_out[15:8]));
  xor xor_2 (xor_2_out, driver_1_out[0], or_1_out);
  nor nor_4 (nor_4_out, xor_2_out, Clock);
  nor nor_5 (nor_5_out, nor_4_out, Reset, nor_2_out);
  and and_5 (and_5_out, nor_5_out, Clock);
  nor nor_6 (nor_6_out, and_5_out, nor_3_out[0]);
  nor nor_7 (nor_7_out, nor_10_out, Clock);
  nor nor_8 (nor_8_out, nor_11_out, nor_7_out);
  and and_6 (and_6_out, Clock, nor_8_out);
  nor nor_9 (nor_3_out[1], nor_12_out, and_6_out);
  xor xor_3 (xor_3_out, driver_1_out[1], Dec);
  and and_7 (and_7_out, xor_3_out, and_3_out);
  nor nor_10 (nor_10_out, xor_4_out, Clock);
  nor nor_11 (nor_11_out, nor_10_out, Reset, nor_8_out);
  and and_8 (and_8_out, nor_11_out, Clock);
  nor nor_12 (nor_12_out, and_8_out, nor_3_out[1]);
  xor xor_4 (xor_4_out, driver_1_out[1], and_3_out);
  xor xor_5 (xor_5_out, driver_1_out[2], Dec);
  and and_9 (and_9_out, xor_5_out, and_7_out);
  nor nor_13 (nor_13_out, nor_16_out, Clock);
  nor nor_14 (nor_14_out, nor_17_out, nor_13_out);
  and and_10 (and_10_out, Clock, nor_14_out);
  nor nor_15 (nor_3_out[2], nor_18_out, and_10_out);
  xor xor_6 (xor_6_out, driver_1_out[2], and_7_out);
  nor nor_16 (nor_16_out, xor_6_out, Clock);
  nor nor_17 (nor_17_out, nor_16_out, Reset, nor_14_out);
  and and_11 (and_11_out, nor_17_out, Clock);
  nor nor_18 (nor_18_out, and_11_out, nor_3_out[2]);
  nor nor_19 (nor_19_out, nor_22_out, Clock);
  nor nor_20 (nor_20_out, nor_23_out, nor_19_out);
  and and_12 (and_12_out, Clock, nor_20_out);
  nor nor_21 (nor_3_out[3], nor_24_out, and_12_out);
  xor xor_7 (xor_7_out, driver_1_out[3], Dec);
  and and_13 (and_13_out, xor_7_out, and_9_out);
  nor nor_22 (nor_22_out, xor_8_out, Clock);
  nor nor_23 (nor_23_out, nor_22_out, Reset, nor_20_out);
  and and_14 (and_14_out, nor_23_out, Clock);
  nor nor_24 (nor_24_out, and_14_out, nor_3_out[3]);
  xor xor_8 (xor_8_out, driver_1_out[3], and_9_out);
  xor xor_9 (xor_9_out, driver_1_out[4], Dec);
  and and_15 (and_15_out, xor_9_out, and_13_out);
  nor nor_25 (nor_25_out, nor_28_out, Clock);
  nor nor_26 (nor_26_out, nor_29_out, nor_25_out);
  and and_16 (and_16_out, Clock, nor_26_out);
  nor nor_27 (nor_3_out[4], nor_30_out, and_16_out);
  xor xor_10 (xor_10_out, driver_1_out[4], and_13_out);
  nor nor_28 (nor_28_out, xor_10_out, Clock);
  nor nor_29 (nor_29_out, nor_28_out, Reset, nor_26_out);
  and and_17 (and_17_out, nor_29_out, Clock);
  nor nor_30 (nor_30_out, and_17_out, nor_3_out[4]);
  nor nor_31 (nor_31_out, nor_34_out, Clock);
  nor nor_32 (nor_32_out, nor_35_out, nor_31_out);
  and and_18 (and_18_out, Clock, nor_32_out);
  nor nor_33 (nor_3_out[5], nor_36_out, and_18_out);
  xor xor_11 (xor_11_out, driver_1_out[5], Dec);
  and and_19 (and_19_out, xor_11_out, and_15_out);
  nor nor_34 (nor_34_out, xor_12_out, Clock);
  nor nor_35 (nor_35_out, nor_34_out, Reset, nor_32_out);
  and and_20 (and_20_out, nor_35_out, Clock);
  nor nor_36 (nor_36_out, and_20_out, nor_3_out[5]);
  xor xor_12 (xor_12_out, driver_1_out[5], and_15_out);
  xor xor_13 (xor_13_out, driver_1_out[6], Dec);
  and and_21 (and_21_out, xor_13_out, and_19_out);
  nor nor_37 (nor_37_out, nor_40_out, Clock);
  nor nor_38 (nor_38_out, nor_41_out, nor_37_out);
  and and_22 (and_22_out, Clock, nor_38_out);
  nor nor_39 (nor_3_out[6], nor_42_out, and_22_out);
  xor xor_14 (xor_14_out, driver_1_out[6], and_19_out);
  nor nor_40 (nor_40_out, xor_14_out, Clock);
  nor nor_41 (nor_41_out, nor_40_out, Reset, nor_38_out);
  and and_23 (and_23_out, nor_41_out, Clock);
  nor nor_42 (nor_42_out, and_23_out, nor_3_out[6]);
  nor nor_43 (nor_43_out, nor_46_out, Clock);
  nor nor_44 (nor_44_out, nor_47_out, nor_43_out);
  and and_24 (and_24_out, Clock, nor_44_out);
  nor nor_45 (nor_3_out[7], nor_48_out, and_24_out);
  xor xor_15 (xor_15_out, driver_1_out[7], Dec);
  and and_25 (Carry, xor_15_out, and_21_out);
  nor nor_46 (nor_46_out, xor_16_out, Clock);
  nor nor_47 (nor_47_out, nor_46_out, Reset, nor_44_out);
  and and_26 (and_26_out, nor_47_out, Clock);
  nor nor_48 (nor_48_out, and_26_out, nor_3_out[7]);
  xor xor_16 (xor_16_out, driver_1_out[7], and_21_out);
endmodule
