// Digital circuit Stack_Pointer_custom.dig as structural Verilog
module Stack_Pointer_custom (
  input  Inc,
  input  Dec,
  input  Reset,
  input  Clock,
  input  CS,
  input  [7:0] Data,
  output Addr,
  output Carry,
  output [7:0] Out
);

  wire and_1_out, and_2_out, and_3_out, and_4_out, and_5_out, and_6_out, and_7_out, or_1_out, xor_1_out,
       xor_3_out, xor_5_out, xor_7_out, xor_9_out, xor_11_out, xor_13_out, xor_15_out;

  or or_1 (or_1_out, Inc, Dec);
  xor xor_1 (xor_1_out, Data[0], Dec);
  and and_1 (and_1_out, xor_1_out, or_1_out);
  xor xor_2 (Out[0], Data[0], or_1_out);
  xor xor_3 (xor_3_out, Data[1], Dec);
  and and_2 (and_2_out, xor_3_out, and_1_out);
  xor xor_4 (Out[1], Data[1], and_1_out);
  xor xor_5 (xor_5_out, Data[2], Dec);
  and and_3 (and_3_out, xor_5_out, and_2_out);
  xor xor_6 (Out[2], Data[2], and_2_out);
  xor xor_7 (xor_7_out, Data[3], Dec);
  and and_4 (and_4_out, xor_7_out, and_3_out);
  xor xor_8 (Out[3], Data[3], and_3_out);
  xor xor_9 (xor_9_out, Data[4], Dec);
  and and_5 (and_5_out, xor_9_out, and_4_out);
  xor xor_10 (Out[4], Data[4], and_4_out);
  xor xor_11 (xor_11_out, Data[5], Dec);
  and and_6 (and_6_out, xor_11_out, and_5_out);
  xor xor_12 (Out[5], Data[5], and_5_out);
  xor xor_13 (xor_13_out, Data[6], Dec);
  and and_7 (and_7_out, xor_13_out, and_6_out);
  xor xor_14 (Out[6], Data[6], and_6_out);
  xor xor_15 (xor_15_out, Data[7], Dec);
  and and_8 (Carry, xor_15_out, and_7_out);
  xor xor_16 (Out[7], Data[7], and_7_out);

  assign Addr = Reset;
endmodule
